# Fritzing sketch Voice Pitcher (saved by Fritzing 0.9.3b)

parts:
  Bauteil1 = Arduino Uno (Rev3)
  Q1 = NPN-Transistor [part_number=BC337-40 package="TO92 [THT]"]
  SP1 = SPEAKER [package=pcb_mount_speaker]
  Bauteil2 = Breakout Board for Electret Microphone
  U1 = POT [package=pot_mammoth]
  C2 = Electrolytic Capacitor [capacitance=1000µF package="300 mil [THT, electrolytic]"]
  SP2 = SPEAKER [package=pcb_mount_speaker]
  R1 = Resistor [tolerance=±5% resistance=1k package="1206 [SMD]"]
  C3 = Ceramic Capacitor [capacitance=100nF package="200 mil [THT, multilayer]"]
  D1 = Diode [package=diode-hv]

nets:
  N1: Bauteil1.A0, Bauteil2.AUD
  N2: Bauteil1.A1, U1.S, C3.1
  N3: Bauteil1.A4/SDA, U1.A, C3.0
  N4: Bauteil1.A5/SCL, U1.E
  GND: Bauteil1.GND, Q1.E, Bauteil2.GND, C2.-
  N5: Bauteil1.D3_PWM, R1.Pin_0
  3V3: Bauteil1.3V3, Bauteil2.VCC
  N6: Bauteil1.5V, SP1.+, C2.+, SP2.+, D1.C
  N7: Q1.B, R1.Pin_1
  N8: Q1.C, D1.A
  N9: SP1.-, SP2.-
